// Logisim project processor.circ as structural Verilog
module xor2 (
  input  i_0,
  input  i_1,
  output o
);

  wire and1_out, and2_out, not1_out, not2_out;

  not not1 (not1_out, i_1);
  not not2 (not2_out, i_0);
  and and1 (and1_out, i_0, not1_out);
  and and2 (and2_out, not2_out, i_1);
  or or1 (o, and1_out, and2_out);
endmodule

module xor8 (
  input  a_0,
  input  a_1,
  input  a_2,
  input  a_3,
  input  a_4,
  input  a_5,
  input  a_6,
  input  a_7,
  input  b_0,
  input  b_1,
  input  b_2,
  input  b_3,
  input  b_4,
  input  b_5,
  input  b_6,
  input  b_7,
  output o_0,
  output o_1,
  output o_2,
  output o_3,
  output o_4,
  output o_5,
  output o_6,
  output o_7
);

  xor2 xor2_1 (.i_0(a_0), .i_1(b_0), .o(o_0));
  xor2 xor2_2 (.i_0(a_1), .i_1(b_1), .o(o_1));
  xor2 xor2_3 (.i_0(a_2), .i_1(b_2), .o(o_2));
  xor2 xor2_4 (.i_0(a_3), .i_1(b_3), .o(o_3));
  xor2 xor2_5 (.i_0(a_4), .i_1(b_4), .o(o_4));
  xor2 xor2_6 (.i_0(a_5), .i_1(b_5), .o(o_5));
  xor2 xor2_7 (.i_0(a_6), .i_1(b_6), .o(o_6));
  xor2 xor2_8 (.i_0(a_7), .i_1(b_7), .o(o_7));
endmodule

module and8 (
  input  [7:0] in_1,
  input  [7:0] in_2,
  output [7:0] out_3
);

  assign out_3 = in_1 & in_2;  // AND_Gate and_1, 8 bits wide
endmodule

module or8 (
  input  [7:0] in_1,
  input  [7:0] in_2,
  output [7:0] out_3
);

  assign out_3 = in_1 | in_2;  // OR_Gate or_1, 8 bits wide
endmodule

module half_add (
  input  in_1,
  input  in_2,
  input  in_3,
  output out_4
);

  xor2 xor2_1 (.i_0(in_1), .i_1(in_2));  // open: o
  xor2 xor2_2 (.i_1(in_3));  // open: i_0, o
endmodule
